# Fritzing sketch IoT_Remote_Light_and_Message_Panel (saved by Fritzing 0.9.3b)
breadboards: 3

parts:
  LCM1602_IIC1 = LCM1602 IIC [part_number="LCM1602 IIC" chip_label="LCM1602 IIC" package="DIP (Dual Inline) [THT]"]
  U2 = 2-Channel 5v Relay Shield [package=relay-2ch5v10a]
  LCD1 = LCD screen
  LED1 = smd LED [color="Red (633nm)" package="0603 [SMD]"]
  U3 = NodeMCU V3.0

nets:
  VSS: LCM1602_IIC1.VSS, LCD1.VSS
  VDD: LCM1602_IIC1.VDD, LCD1.VDD
  N1: LCM1602_IIC1.V0, LCD1.V0
  N2: LCM1602_IIC1.RS, LCD1.RS
  N3: LCM1602_IIC1.RW, LCD1.R/W
  N4: LCM1602_IIC1.E, LCD1.E
  N5: LCM1602_IIC1.D0, LCD1.DB0
  N6: LCM1602_IIC1.D1, LCD1.DB1
  N7: LCM1602_IIC1.D2, LCD1.DB2
  N8: LCM1602_IIC1.D3, LCD1.DB3
  N9: LCM1602_IIC1.D4, LCD1.DB4
  N10: LCM1602_IIC1.D5, LCD1.DB5
  N11: LCM1602_IIC1.D6, LCD1.DB6
  N12: LCM1602_IIC1.D7, LCD1.DB7
  N13: LCM1602_IIC1.A, LCD1.LED+
  N14: LCM1602_IIC1.K, LCD1.LED-
  GND: LCM1602_IIC1.GND, U2.GND, U3.GND#41
  VCC: LCM1602_IIC1.VCC, LCM1602_IIC1.SDA, LCM1602_IIC1.SCL, U2.VCC, U3.D1, U3.D2, U3.VU
  N15: LCM1602_IIC1.LED_A, LCM1602_IIC1.LED_B
  N16: U2.IN1, U3.D4
  N17: LED1.cathode, U3.D7
  N18: LED1.anode, U3.GND#6, U3.GND#13, U3.GND#16, U3.GND#33

custom parts:
  LCM1602 IIC: I2C-Module to use a 1602 or 2004 LCD on with the wire.h libory Serial LCD Modul
  2-Channel 5v Relay Shield: 2 Channel 5v Relay Shield w. 2x SPD-06VDC-SD-C
  NodeMCU V3.0: ESP8266 based NodeMCU
